# Fritzing sketch bigSound (saved by Fritzing 0.9.3b)
breadboards: 1

parts:
  Mic1 = KY-038
  U1 = ESP32S-HiLetgo [part_number=ESP32S-HiLetgo]
  LED1 = LED - 5mm [color="Red (633nm)" package="5 mm [THT]"]
  R1 = Resistor [tolerance=±5% resistance=220 package=THT]

nets:
  N1: Mic1.pin1, U1.GPIO4
  N2: Mic1.pin2, U1.GND, R1.Pin_1
  N3: Mic1.pin3, U1.3.3
  N4: Mic1.pin4, U1.GPIO0
  N5: U1.GPIO36, LED1.cathode
  N6: LED1.anode, R1.Pin_0

custom parts:
  KY-038: ky-038 Microphone sound sensor module
  ESP32S-HiLetgo: HiLetgo ESP-WROOM-32 ESP32 ESP-32S Development Board 2.4GHz Dual-Mode WiFi + Bluetooth Dual Cores Microcontroller The ESP32 integrated with Antenna switches, RF Balun, power amplifiers, low-noise amplifiers, filters, and management modules, and the entire solution occupies the least area of PCB. 2.4 GHz Wi-Fi plus Bluetooth dual-mode chip, with TSMC Ultra-low power consumption 40nm technology,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
