# Fritzing sketch oled (saved by Fritzing 0.9.3b)
breadboards: 1

parts:
  OLED_I2C1 = OLED 128x64 I2C Monochrome Display
  U1 = ESP32S-HiLetgo [part_number=ESP32S-HiLetgo]
  S1 = Momentary Switch [package=ksa_sealed_tac_switch]
  R1 = Resistor [tolerance=±5% resistance=220 package=THT]

nets:
  N1: OLED_I2C1.SDA, U1.GPIO22
  N2: OLED_I2C1.SCK, U1.GPIO23
  N3: OLED_I2C1.VDD, U1.3.3, R1.Pin_0
  GND: OLED_I2C1.GND, U1.GND, S1.1
  N4: U1.GPIO2, S1.3, R1.Pin_1

custom parts:
  ESP32S-HiLetgo: HiLetgo ESP-WROOM-32 ESP32 ESP-32S Development Board 2.4GHz Dual-Mode WiFi + Bluetooth Dual Cores Microcontroller The ESP32 integrated with Antenna switches, RF Balun, power amplifiers, low-noise amplifiers, filters, and management modules, and the entire solution occupies the least area of PCB. 2.4 GHz Wi-Fi plus Bluetooth dual-mode chip, with TSMC Ultra-low power consumption 40nm technology,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

// code stored in the sketch: Oled.ino
#include <Wire.h>
#include <Adafruit_GFX.h>
#include <Adafruit_SSD1306.h>

#define SCREEN_WIDTH 128 // OLED display width, in pixels
#define SCREEN_HEIGHT 64 // OLED display height, in pixels
const int boton = 2;

// Declaration for an SSD1306 display connected to I2C (SDA, SCL pins)
Adafruit_SSD1306 display(SCREEN_WIDTH, SCREEN_HEIGHT, &Wire, -1);

void setup() {
  Serial.begin(115200);

  if(!display.begin(SSD1306_SWITCHCAPVCC, 0x3C)) { // Address 0x3D for 128x64
    Serial.println(F("SSD1306 allocation failed"));
    for(;;);
  }
  delay(2000);
  display.clearDisplay();

  display.setTextSize(1);
  display.setTextColor(WHITE);
  display.setCursor(0, 10);
  display.display(); 
pinMode(boton, INPUT_PULLUP);
}

void loop() {

while(digitalRead(boton) == HIGH);

display.clearDisplay();
display.setCursor(0,10);
display.print("Sandra Chiquito");
display.display();

while(digitalRead(boton) == LOW);

  
}
