# Fritzing sketch reed switch (saved by Fritzing 0.9.3b)
breadboards: 1

parts:
  Mod1 = KY-025 Reed Switch Module [package="Breakout board"]
  U1 = ESP32S-HiLetgo [part_number=ESP32S-HiLetgo]

nets:
  N1: Mod1.A0, U1.GPIO2
  N2: Mod1.G, U1.GND
  N3: Mod1.+, U1.3.3
  N4: Mod1.D0, U1.GPIO4

custom parts:
  KY-025 Reed Switch Module: KY-025 Reed Switch Module, it reacts in the presence of a magnetic field.
  ESP32S-HiLetgo: HiLetgo ESP-WROOM-32 ESP32 ESP-32S Development Board 2.4GHz Dual-Mode WiFi + Bluetooth Dual Cores Microcontroller The ESP32 integrated with Antenna switches, RF Balun, power amplifiers, low-noise amplifiers, filters, and management modules, and the entire solution occupies the least area of PCB. 2.4 GHz Wi-Fi plus Bluetooth dual-mode chip, with TSMC Ultra-low power consumption 40nm technology,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

// code stored in the sketch: reed switch.fzz.ino
int analogPin = 4; 
int digitalPin = 2;

void setup() {
  pinMode(analogPin, INPUT); 
  pinMode(digitalPin, INPUT); 
  Serial.begin(9600);
}

void loop() {
  int analogVal = analogRead(analogPin);
  int digitalVal = digitalRead(digitalPin);
  
  Serial.print(analogVal);
  Serial.print(" - ");
  Serial.println(digitalVal);
  
  delay(100);
}
