# Fritzing sketch RotaryEncoder (saved by Fritzing 0.9.3b)
breadboards: 1

parts:
  RE2 = KY-040 Rotary encoder [package=THT]
  U1 = ESP32S-HiLetgo [part_number=ESP32S-HiLetgo]

nets:
  N1: RE2.DT, U1.GPIO23
  N2: RE2.CLK, U1.GPIO22

custom parts:
  KY-040 Rotary encoder: KY-040 Rotary Encoder with switch on breakout borad from AZ Delivery
  ESP32S-HiLetgo: HiLetgo ESP-WROOM-32 ESP32 ESP-32S Development Board 2.4GHz Dual-Mode WiFi + Bluetooth Dual Cores Microcontroller The ESP32 integrated with Antenna switches, RF Balun, power amplifiers, low-noise amplifiers, filters, and management modules, and the entire solution occupies the least area of PCB. 2.4 GHz Wi-Fi plus Bluetooth dual-mode chip, with TSMC Ultra-low power consumption 40nm technology,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

// code stored in the sketch: RotaryEncoder.fzz.ino
#include "AiEsp32RotaryEncoder.h"
#include "Arduino.h"

#define ROTARY_ENCODER_A_PIN 23
#define ROTARY_ENCODER_B_PIN 22
#define ROTARY_ENCODER_BUTTON_PIN 21
#define ROTARY_ENCODER_VCC_PIN -1
#define ROTARY_ENCODER_STEPS 4

//instead of changing here, rather change numbers above
AiEsp32RotaryEncoder rotaryEncoder = AiEsp32RotaryEncoder(ROTARY_ENCODER_A_PIN, ROTARY_ENCODER_B_PIN, ROTARY_ENCODER_BUTTON_PIN, ROTARY_ENCODER_VCC_PIN, ROTARY_ENCODER_STEPS);

void rotary_onButtonClick()
{
    static unsigned long lastTimePressed = 0; // Soft debouncing
    if (millis() - lastTimePressed < 500)
    {
            return;
    }
    lastTimePressed = millis();
    Serial.print("button pressed ");
    Serial.print(millis());
    Serial.println(" milliseconds after restart");
}

void rotary_loop()
{
    //dont print anything unless value changed
    if (rotaryEncoder.encoderChanged())
    {
            Serial.print("Value: ");
            Serial.println(rotaryEncoder.readEncoder());
    }
    if (rotaryEncoder.isEncoderButtonClicked())
    {
            rotary_onButtonClick();
    }
}

void IRAM_ATTR readEncoderISR()
{
    rotaryEncoder.readEncoder_ISR();
}

void setup()
{
    Serial.begin(115200);

    //we must initialize rotary encoder
    rotaryEncoder.begin();
    rotaryEncoder.setup(readEncoderISR);
    //set boundaries and if values should cycle or not
    //in this example we will set possible values between 0 and 1000;
    bool circleValues = false;
    rotaryEncoder.setBoundaries(0, 1000, circleValues); //minValue, maxValue, circleValues true|false (when max go to min and vice versa)

    /*Rotary acceleration introduced 25.2.2021.
   * in case range to select is huge, for example - select a value between 0 and 1000 and we want 785
   * without accelerateion you need long time to get to that number
   * Using acceleration, faster you turn, faster will the value raise.
   * For fine tuning slow down.
   */
    //rotaryEncoder.disableAcceleration(); //acceleration is now enabled by default - disable if you dont need it
    rotaryEncoder.setAcceleration(250); //or set the value - larger number = more accelearation; 0 or 1 means disabled acceleration
}

void loop()
{
    //in loop call your custom function which will process rotary encoder values
    rotary_loop();
    delay(50); //or do whatever you need to do...
}
